// Logisim project Dual_dice.circ as structural Verilog: 1 circuit, main circuit main
module main (
  input  in_1,
  input  in_2,
  input  in_3,
  input  in_4,
  input  in_5,
  output [3:0] PIN,
  output out_7,
  output out_8,
  output out_9,
  output out_10,
  output out_11
);

  wire clock_1_out, clock_2_out, clock_3_out, decoder_1_out1, decoder_1_out2, decoder_1_out3, decoder_1_out4,
       decoder_1_out5, decoder_1_out6, decoder_2_out1, decoder_2_out2, decoder_2_out3, decoder_2_out4,
       decoder_2_out5, decoder_2_out6;
  wire [2:0] random_1_out, random_2_out, random_3_out;
  wire [3:0] adder_2_out, bit_extender_1_out, bit_extender_2_out, bit_extender_3_out, counter_1_q;
  wire [7:0] bit_extender_4_out, bit_extender_5_out;

  Clock clock_1 (.out(clock_1_out));
  Counter #(.width(4), .max('h6)) counter_1 (
    .count(in_2), .Q(counter_1_q), .clk(clock_1_out));  // open: load, D, carry, clr
  Decoder #(.select(4)) decoder_1 (
    .out1(decoder_1_out1), .out2(decoder_1_out2), .out3(decoder_1_out3), .out4(decoder_1_out4),
    .out5(decoder_1_out5), .out6(decoder_1_out6), .sel(counter_1_q), .en(in_1));  // open: out0, out7, out8, out9, out10, out11, out12, out13, out14, out15
  Clock clock_2 (.out(clock_2_out));
  Random #(.width(3)) random_1 (.clk(clock_2_out), .next(in_4), .out(random_1_out));  // open: clr
  Decoder #(.select(3)) decoder_2 (
    .out1(decoder_2_out1), .out2(decoder_2_out2), .out3(decoder_2_out3), .out4(decoder_2_out4),
    .out5(decoder_2_out5), .out6(decoder_2_out6), .sel(random_1_out), .en(in_3));  // open: out0, out7
  assign bit_extender_1_out = {{1{1'b0}}, random_2_out};  // Bit_Extender bit_extender_1
  Random #(.width(3)) random_2 (.clk(clock_1_out), .next(in_5), .out(random_2_out));  // open: clr
  assign bit_extender_2_out = {{1{1'b0}}, random_1_out};  // Bit_Extender bit_extender_2
  Adder #(.width(4)) adder_1 (.a(bit_extender_2_out), .b(counter_1_q), .out(PIN), .cout(out_7));  // open: cin
  assign bit_extender_3_out = {{1{1'b0}}, random_3_out};  // Bit_Extender bit_extender_3
  Adder #(.width(4)) adder_2 (
    .a(bit_extender_1_out), .b(bit_extender_3_out), .out(adder_2_out), .cout(out_11));  // open: cin
  Clock clock_3 (.out(clock_3_out));
  Random #(.width(3)) random_3 (.clk(clock_3_out), .next(in_5), .out(random_3_out));  // open: clr
  LED _1 (.in(decoder_1_out1));
  LED _1_2 (.in(decoder_2_out1));
  LED _2 (.in(decoder_1_out2));
  LED _2_2 (.in(decoder_2_out2));
  assign bit_extender_4_out = {{4{1'b0}}, PIN};  // Bit_Extender bit_extender_4
  LED _3 (.in(decoder_1_out3));
  LED _4 (.in(decoder_1_out4));
  LED _3_2 (.in(decoder_2_out3));
  Comparator #(.width(4), .mode("unsigned")) comparator_1 (
    .a(PIN), .b(adder_2_out), .gt(out_8), .eq(out_9), .lt(out_10));
  LED _5 (.in(decoder_1_out5));
  LED _5_2 (.in(decoder_2_out5));
  LED _4_2 (.in(decoder_2_out4));
  assign bit_extender_5_out = {{4{1'b0}}, adder_2_out};  // Bit_Extender bit_extender_5
  LED _6 (.in(decoder_1_out6));
  LED _6_2 (.in(decoder_2_out6));
  Hex_Digit_Display hex_digit_display_1 (.value(bit_extender_4_out[3:0]));  // open: dp
  Hex_Digit_Display hex_digit_display_2 (.value(bit_extender_4_out[7:4]));  // open: dp
  Hex_Digit_Display hex_digit_display_3 (.value(bit_extender_5_out[7:4]));  // open: dp
  Hex_Digit_Display hex_digit_display_4 (.value(bit_extender_5_out[3:0]));  // open: dp

  // Notes on the sheet:
  //   CLOCK
  //   COUNTER
  //   4-BIT
  //   DECODER
  //   with counter and decoder we make LED CHASER
  //   DECODER
  //   RANDOM GENERATOR
  //   Random generator
  //   BIT EXTENDER
  //   4-BIT ADDER
  //   adding two bitrandom generator number
  //   ADDER
  //   6-LED
  //   clock
  //   6-LED
  //   Random number generator in led
  //   RANDOM GENERATOR
  //   BIT EXTENDER
  //   COMPARE 2-bit number 
  //   two random number generator
  //   COMPARATOR
  //   with the comparator
  //   LED CHASER
  //   SPLITTER
  //   7-SEGMENT Display
  //   final result
  //   IF BOTH ARE EQUAL, THIS GLOWS
  //   IF LED NUMVER SUM IS BIGGER, THIS GLOWS
  //   IF RANDOM NUMBERS SUM IS BIGGER, THIS GLOWS
endmodule
